// Digital circuit Decode Logic.dig as structural Verilog
module Decode_Logic (
  input  A15,
  input  A14,
  input  A13,
  input  A12,
  input  A11,
  input  nWR,
  input  nMREQ,
  input  nM1,
  input  nIOREQ,
  output IOWRI,
  output nBANK,
  output nRAM,
  output nROM
);

  wire and_3_out, demultiplexer_1_out_0, demultiplexer_1_out_1, demultiplexer_1_out_3, demultiplexer_2_out_3,
       not_1_out, not_2_out, or_1_out;

  or or_1 (or_1_out, nMREQ, A15);
  not not_1 (not_1_out, nWR);
  not not_2 (not_2_out, nIOREQ);
  Demultiplexer #(.Selector_Bits(2), .Default(1)) demultiplexer_1 (
    .sel({A14, A13}), .in(or_1_out), .out_0(demultiplexer_1_out_0), .out_1(demultiplexer_1_out_1),
    .out_3(demultiplexer_1_out_3));  // open: out_2
  and and_1 (IOWRI, nM1, not_1_out, not_2_out);
  and and_2 (nROM, demultiplexer_1_out_0, demultiplexer_1_out_1);
  Demultiplexer #(.Selector_Bits(2), .Default(1)) demultiplexer_2 (
    .sel({A12, A11}), .in(demultiplexer_1_out_3), .out_3(demultiplexer_2_out_3));  // open: out_0, out_1, out_2
  and and_3 (and_3_out, A15, ~nMREQ);  // And
  nand nand_1 (nBANK, A15, A14);
  and and_4 (nRAM, ~and_3_out, demultiplexer_2_out_3);  // And

  // Notes on the sheet:
  //   A15: pin 1
  //   A14: pin 2
  //   A13: pin 3
  //   A12: pin 4
  //   A11: pin 5
  //   nWR: pin 9
  //   nMREQ: pin 10
  //   nM1: pin 11
  //   nIOREQ: pin 13
  //   IOWRI: pin 23
  //   nBANK: pin 22
  //   nRAM: pin 18
  //   nROM: pin 17
endmodule
